# Fritzing sketch WS2812B (saved by Fritzing 0.9.3b)

parts:
  NEOPIXEL1 = Neopixel Strip -- White (30/m)
  Part2 = Arduino Nano (Rev3.0) (ICSP)
  Raspberry_Pi_1 = Raspberry Pi 3 [part_number=RPI-3-V1.2]  # not connected

nets:
  GND: NEOPIXEL1.GND, Part2.GND
  N1: NEOPIXEL1.Din, Part2.D2
  +5V: NEOPIXEL1.+5V, Part2.5V

custom parts:
  Neopixel Strip -- White (30/m): These NeoPixel strips have 30 digitally-addressable pixel LEDs per meter and are very affordable and are only 12.5 mm wide, 10 mm if you remove the strip from the casing.
