# Fritzing sketch schematics (saved by Fritzing 0.9.3b)

parts:
  Part1 = SparkFun ESP8266 Thing
  NEOPIXEL1 = Neopixel Strip -- White (30/m)

nets:
  N1: Part1.USBVCC, NEOPIXEL1.+5V
  GND: Part1.GND, NEOPIXEL1.GND
  N2: Part1.GPIO5, NEOPIXEL1.Din

custom parts:
  Neopixel Strip -- White (30/m): These NeoPixel strips have 30 digitally-addressable pixel LEDs per meter and are very affordable and are only 12.5 mm wide, 10 mm if you remove the strip from the casing.
